# Fritzing sketch rilevatore_gas_scheme (saved by Fritzing 0.9.3b)
breadboards: 1

parts:
  IR_Receiver = TSOP312.., 314.. [package=THT]
  MQ-7 = MQ-7 breakout
  LCD1 = LCD screen
  LED1 = LED - 5mm [color="Yellow (595nm)" package="5 mm [THT]"]
  LED3 = LED - 5mm [color="Green (560nm)" package="5 mm [THT]"]
  MQ-4 = MQ-4
  Potenziometro = Rotary Potentiometer (Small) [maximum_resistance=100kΩ package=THT]
  R4 = Resistor [tolerance=±5% resistance=220 package=THT]
  R2 = Resistor [tolerance=±5% resistance=220 package=THT]
  LED2 = LED - 5mm [color="Red (633nm)" package="5 mm [THT]"]
  MQ-3 = MQ-3 breakout
  SG1 = Buzzer 12mm [package=buzzer-12mm-ns]
  part = Arduino Uno (Rev3)
  R3 = Resistor [tolerance=±5% resistance=220 package=THT]

nets:
  GND: IR_Receiver.GND, MQ-7.GND, LCD1.VSS, LCD1.R/W, LCD1.LED-, MQ-4.GND, Potenziometro.leg2, R4.Pin_0, R2.Pin_0, MQ-3.GND, SG1.2, part.GND, R3.Pin_0
  VCC: IR_Receiver.Vs, MQ-7.VCC, LCD1.VDD, LCD1.LED+, MQ-4.VCC, Potenziometro.leg1, MQ-3.VCC, part.5V
  N1: IR_Receiver.Data, part.D6_PWM
  N2: MQ-7.DO, part.D1/TX
  N3: MQ-7.AO, part.A4/SDA
  N4: LCD1.V0, Potenziometro.wiper
  N5: LCD1.RS, part.D7
  N6: LCD1.E, part.D8
  N7: LCD1.DB4, part.D9_PWM
  N8: LCD1.DB5, part.D10_PWM/SS
  N9: LCD1.DB6, part.D11_PWM/MOSI
  N10: LCD1.DB7, part.D12/MISO
  N11: LED1.cathode, R4.Pin_1
  N12: LED1.anode, part.D4
  N13: LED3.cathode, R3.Pin_1
  N14: LED3.anode, part.D3_PWM
  N15: MQ-4.DO, part.D0/RX
  N16: MQ-4.AO, part.A3
  N17: R2.Pin_1, LED2.cathode
  N18: LED2.anode, part.D5_PWM
  N19: MQ-3.DO, part.D2
  N20: MQ-3.AO, part.A5/SCL
  N21: SG1.1, part.D13/SCK

custom parts:
  MQ-7 breakout: SKU: 101282
  MQ-3 breakout: Alcohol sensor is capable of detecting alcohol (ethanol) particles on itself and gives the information in digital form back to us to manipulate with it. SKU:101251 • Voltage: 5V DC • Power: max 750mW • Measurement range: 0.04-4mg/L
